// Logisim project ex4.circ as structural Verilog: 1 circuit, main circuit main
module main (
  input  A,
  input  B,
  input  C,
  output Y
);

  wire not_1_out, or_1_out;

  not not_1 (not_1_out, B);
  or or_1 (or_1_out, not_1_out, C);
  and and_1 (Y, A, or_1_out);
endmodule
