// Logisim project ex5.circ as structural Verilog: 1 circuit, main circuit main
module main (
  input  A2,
  input  A1,
  input  A0,
  output Y6,
  output Y5,
  output Y4,
  output Y3,
  output Y2,
  output Y1,
  output Y0
);

  wire and_1_out, and_2_out, and_3_out;

  and and_1 (and_1_out, A0, A1);
  and and_2 (and_2_out, A0, A2);
  and and_3 (and_3_out, A1, A2);
  or or_1 (Y0, A0, A1, A2);
  or or_2 (Y1, A1, A2);
  or or_3 (Y2, and_1_out, A2);
  or or_4 (Y4, and_2_out, and_3_out);
  and and_4 (Y5, A1, A2);
  and and_5 (Y6, A0, A1, A2);

  assign Y3 = A2;
endmodule
